// Logisim project Lab05_1.circ as structural Verilog: 2 circuits, main circuit main
module main (
  input  [3:0] ABCD
);

  wire bcd_7seg_decoder_1_c0, bcd_7seg_decoder_1_c1, bcd_7seg_decoder_1_c2, bcd_7seg_decoder_1_c3,
       bcd_7seg_decoder_1_c4, bcd_7seg_decoder_1_c5, bcd_7seg_decoder_1_c6;

  BCD_7Seg_Decoder bcd_7seg_decoder_1 (
    .ABCD(ABCD), .C0(bcd_7seg_decoder_1_c0), .C1(bcd_7seg_decoder_1_c1), .C2(bcd_7seg_decoder_1_c2),
    .C3(bcd_7seg_decoder_1_c3), .C4(bcd_7seg_decoder_1_c4), .C5(bcd_7seg_decoder_1_c5),
    .C6(bcd_7seg_decoder_1_c6));
  _7_Segment_Display u_7_segment_display_1 (
    .g(bcd_7seg_decoder_1_c6), .f(bcd_7seg_decoder_1_c5), .a(bcd_7seg_decoder_1_c0),
    .b(bcd_7seg_decoder_1_c1), .e(bcd_7seg_decoder_1_c4), .d(bcd_7seg_decoder_1_c3), .c(bcd_7seg_decoder_1_c2));  // open: dp

  // Notes on the sheet:
  //   BCD to 7-Segment Decoder
endmodule

module BCD_7Seg_Decoder (
  input  [3:0] ABCD,
  output C0,
  output C1,
  output C2,
  output C3,
  output C4,
  output C5,
  output C6
);

  wire B_prime_C_2_out, B_prime_C_out, B_prime_D_prime_2_out, B_prime_D_prime_3_out, B_prime_D_prime_out,
       BC_prime_2_out, BC_prime_out, BD_out, BD_prime_out, C_prime_D_prime_2_out, C_prime_D_prime_out,
       C_prime_DB_out, CD_out, CD_prime_2_out, CD_prime_3_out, CD_prime_out, not_1_out, not_2_out, not_3_out;

  not not_1 (not_1_out, ABCD[2]);
  not not_2 (not_2_out, ABCD[1]);
  not not_3 (not_3_out, ABCD[0]);
  and B_prime_D_prime (B_prime_D_prime_out, not_1_out, not_3_out);
  and BD (BD_out, ABCD[2], ABCD[0]);
  and C_prime_D_prime (C_prime_D_prime_out, not_2_out, not_3_out);
  and CD (CD_out, ABCD[1], ABCD[0]);
  and B_prime_C (B_prime_C_out, not_1_out, ABCD[1]);
  and B_prime_D_prime_2 (B_prime_D_prime_2_out, not_1_out, not_3_out);
  and CD_prime (CD_prime_out, ABCD[1], not_3_out);
  and C_prime_DB (C_prime_DB_out, not_2_out, ABCD[0], ABCD[2]);
  and B_prime_D_prime_3 (B_prime_D_prime_3_out, not_1_out, not_3_out);
  and CD_prime_2 (CD_prime_2_out, ABCD[1], not_3_out);
  and C_prime_D_prime_2 (C_prime_D_prime_2_out, not_2_out, not_3_out);
  and BC_prime (BC_prime_out, ABCD[2], not_2_out);
  and BD_prime (BD_prime_out, ABCD[2], not_3_out);
  and B_prime_C_2 (B_prime_C_2_out, not_1_out, ABCD[1]);
  and BC_prime_2 (BC_prime_2_out, not_2_out, ABCD[2]);
  and CD_prime_3 (CD_prime_3_out, ABCD[1], not_3_out);
  or or_1 (C0, B_prime_D_prime_out, ABCD[1], ABCD[3], BD_out);
  or or_2 (C1, C_prime_D_prime_out, ABCD[3], not_1_out, CD_out);
  or C_prime_D_B (C2, not_2_out, ABCD[0], ABCD[2]);
  or or_3 (C3, B_prime_C_out, B_prime_D_prime_2_out, CD_prime_out, C_prime_DB_out);
  or or_4 (C4, B_prime_D_prime_3_out, CD_prime_2_out);
  or or_5 (C5, C_prime_D_prime_2_out, ABCD[3], BC_prime_out, BD_prime_out);
  or or_6 (C6, B_prime_C_2_out, ABCD[3], BC_prime_2_out, CD_prime_3_out);
endmodule
