// Logisim project Lab05_2.circ as structural Verilog: 3 circuits, main circuit main
module main (
  input  W,
  input  X,
  input  Y,
  input  Z
);

  wire bcd_7seg_decoder_1_c0, bcd_7seg_decoder_1_c1, bcd_7seg_decoder_1_c2, bcd_7seg_decoder_1_c3,
       bcd_7seg_decoder_1_c4, bcd_7seg_decoder_1_c5, bcd_7seg_decoder_1_c6, bcd_7seg_decoder_2_c0,
       bcd_7seg_decoder_2_c1, bcd_7seg_decoder_2_c2, bcd_7seg_decoder_2_c3, bcd_7seg_decoder_2_c4,
       bcd_7seg_decoder_2_c5, bcd_7seg_decoder_2_c6, multiplier_1_g0, multiplier_1_g1, multiplier_1_g2,
       multiplier_1_g3, multiplier_1_h0, multiplier_1_h1, multiplier_1_h2, multiplier_1_h3;

  Multiplier multiplier_1 (
    .W(W), .X(X), .Y(Y), .Z(Z), .G0(multiplier_1_g0), .G1(multiplier_1_g1), .G2(multiplier_1_g2),
    .G3(multiplier_1_g3), .H0(multiplier_1_h0), .H1(multiplier_1_h1), .H2(multiplier_1_h2),
    .H3(multiplier_1_h3));
  BCD_7Seg_Decoder bcd_7seg_decoder_1 (
    .A(multiplier_1_g3), .B(multiplier_1_g2), .C(multiplier_1_g1), .D(multiplier_1_g0),
    .C0(bcd_7seg_decoder_1_c0), .C1(bcd_7seg_decoder_1_c1), .C2(bcd_7seg_decoder_1_c2),
    .C3(bcd_7seg_decoder_1_c3), .C4(bcd_7seg_decoder_1_c4), .C5(bcd_7seg_decoder_1_c5),
    .C6(bcd_7seg_decoder_1_c6));
  BCD_7Seg_Decoder bcd_7seg_decoder_2 (
    .A(multiplier_1_h3), .B(multiplier_1_h2), .C(multiplier_1_h1), .D(multiplier_1_h0),
    .C0(bcd_7seg_decoder_2_c0), .C1(bcd_7seg_decoder_2_c1), .C2(bcd_7seg_decoder_2_c2),
    .C3(bcd_7seg_decoder_2_c3), .C4(bcd_7seg_decoder_2_c4), .C5(bcd_7seg_decoder_2_c5),
    .C6(bcd_7seg_decoder_2_c6));
  _7_Segment_Display u_7_segment_display_1 (
    .g(bcd_7seg_decoder_1_c6), .f(bcd_7seg_decoder_1_c5), .a(bcd_7seg_decoder_1_c0),
    .b(bcd_7seg_decoder_1_c1), .e(bcd_7seg_decoder_1_c4), .d(bcd_7seg_decoder_1_c3), .c(bcd_7seg_decoder_1_c2));  // open: dp
  _7_Segment_Display u_7_segment_display_2 (
    .g(bcd_7seg_decoder_2_c6), .f(bcd_7seg_decoder_2_c5), .a(bcd_7seg_decoder_2_c0),
    .b(bcd_7seg_decoder_2_c1), .e(bcd_7seg_decoder_2_c4), .d(bcd_7seg_decoder_2_c3), .c(bcd_7seg_decoder_2_c2));  // open: dp

  // Notes on the sheet:
  //   วงจรทวีคูณ
  //   BCD to 7-Segment Decoder
  //   BCD to 7-Segment Decoder
  //   7-Segment Display
  //   หลักสิบ
  //   7-Segment Display
  //   หลักหน่วย
endmodule

module BCD_7Seg_Decoder (
  input  A,
  input  B,
  input  C,
  input  D,
  output C0,
  output C1,
  output C2,
  output C3,
  output C4,
  output C5,
  output C6
);

  wire B_prime_C_2_out, B_prime_C_out, B_prime_D_prime_2_out, B_prime_D_prime_3_out, B_prime_D_prime_out,
       BC_prime_2_out, BC_prime_out, BD_out, BD_prime_out, C_prime_D_prime_2_out, C_prime_D_prime_out,
       C_prime_DB_out, CD_out, CD_prime_2_out, CD_prime_3_out, CD_prime_out, not_1_out, not_2_out, not_3_out;

  not not_1 (not_1_out, B);
  not not_2 (not_2_out, C);
  not not_3 (not_3_out, D);
  and B_prime_D_prime (B_prime_D_prime_out, not_1_out, not_3_out);
  and BD (BD_out, B, D);
  and C_prime_D_prime (C_prime_D_prime_out, not_2_out, not_3_out);
  and CD (CD_out, C, D);
  and B_prime_C (B_prime_C_out, not_1_out, C);
  and B_prime_D_prime_2 (B_prime_D_prime_2_out, not_1_out, not_3_out);
  and CD_prime (CD_prime_out, C, not_3_out);
  and C_prime_DB (C_prime_DB_out, not_2_out, D, B);
  and B_prime_D_prime_3 (B_prime_D_prime_3_out, not_1_out, not_3_out);
  and CD_prime_2 (CD_prime_2_out, C, not_3_out);
  and C_prime_D_prime_2 (C_prime_D_prime_2_out, not_2_out, not_3_out);
  and BC_prime (BC_prime_out, B, not_2_out);
  and BD_prime (BD_prime_out, B, not_3_out);
  and B_prime_C_2 (B_prime_C_2_out, not_1_out, C);
  and BC_prime_2 (BC_prime_2_out, not_2_out, B);
  and CD_prime_3 (CD_prime_3_out, C, not_3_out);
  or or_1 (C0, B_prime_D_prime_out, C, A, BD_out);
  or or_2 (C1, C_prime_D_prime_out, A, not_1_out, CD_out);
  or C_prime_D_B (C2, not_2_out, D, B);
  or or_3 (C3, B_prime_C_out, B_prime_D_prime_2_out, CD_prime_out, C_prime_DB_out);
  or or_4 (C4, B_prime_D_prime_3_out, CD_prime_2_out);
  or or_5 (C5, C_prime_D_prime_2_out, A, BC_prime_out, BD_prime_out);
  or or_6 (C6, B_prime_C_2_out, A, BC_prime_2_out, CD_prime_3_out);
endmodule

module Multiplier (
  input  W,
  input  X,
  input  Y,
  input  Z,
  output G0,
  output G1,
  output G2,
  output G3,
  output H0,
  output H1,
  output H2,
  output H3
);

  wire not_1_out, not_2_out, not_3_out, not_4_out, W_prime_X_prime_Y_out, W_prime_X_prime_Z_out,
       W_prime_XY_out, W_prime_XY_prime_Z_prime_out, W_prime_XYZ_prime_out, W_prime_XZ_out, W_prime_YZ_out,
       WX_out, WX_prime_Y_prime_out, WX_prime_Y_prime_Z_out, WX_prime_Y_prime_Z_prime_out, WX_prime_YZ_out,
       WXY_prime_out, WXY_prime_Z_out, WXYZ_prime_out, WY_out, WY_prime_Z_prime_out, XYZ_out;

  not not_1 (not_1_out, W);
  not not_2 (not_2_out, Y);
  not not_3 (not_3_out, X);
  not not_4 (not_4_out, Z);
  and WX_prime_Y_prime (WX_prime_Y_prime_out, W, not_3_out, not_2_out);
  and XYZ (XYZ_out, X, Y, Z);
  and W_prime_XY (W_prime_XY_out, not_1_out, X, Y);
  and W_prime_XZ (W_prime_XZ_out, not_1_out, X, Z);
  and WX (WX_out, W, X);
  and WY (WY_out, W, Y);
  and WXY_prime_Z (WXY_prime_Z_out, W, X, not_2_out, Z);
  and WX_prime_YZ (WX_prime_YZ_out, W, not_3_out, Y, Z);
  and W_prime_XYZ_prime (W_prime_XYZ_prime_out, not_1_out, X, Y, not_4_out);
  and W_prime_X_prime_Z (W_prime_X_prime_Z_out, not_1_out, not_3_out, Z);
  and WX_prime_Y_prime_Z_prime (WX_prime_Y_prime_Z_prime_out, W, not_3_out, not_2_out, not_4_out);
  and WY_prime_Z_prime (WY_prime_Z_prime_out, W, not_2_out, not_4_out);
  and WXY_prime (WXY_prime_out, W, X, not_2_out);
  and W_prime_YZ (W_prime_YZ_out, not_1_out, Y, Z);
  and W_prime_X_prime_Y (W_prime_X_prime_Y_out, not_1_out, not_3_out, Y);
  and WX_prime_Y_prime_Z (WX_prime_Y_prime_Z_out, W, not_3_out, not_2_out, Z);
  and W_prime_XY_prime_Z_prime (W_prime_XY_prime_Z_prime_out, not_1_out, X, not_2_out, not_4_out);
  and WXYZ_prime (WXYZ_prime_out, W, X, Y, not_4_out);
  or or_1 (G0, WX_prime_Y_prime_out, XYZ_out, W_prime_XY_out, W_prime_XZ_out);
  or or_2 (G1, WX_out, WY_out);
  or or_3 (H1, WXY_prime_Z_out, WX_prime_YZ_out, W_prime_XYZ_prime_out, W_prime_X_prime_Z_out, WX_prime_Y_prime_Z_prime_out);
  or or_4 (H2, WY_prime_Z_prime_out, WXY_prime_out, W_prime_YZ_out, W_prime_X_prime_Y_out);
  or or_5 (H3, WX_prime_Y_prime_Z_out, W_prime_XY_prime_Z_prime_out, WXYZ_prime_out);

  assign G2 = 1'b0;
  assign G3 = 1'b0;
  assign H0 = 1'b0;
endmodule
