// Logisim project Lab05_4.circ as structural Verilog: 2 circuits, main circuit main
module main (
  input  X,
  input  Y,
  input  Z
);

  wire alpha_7seg_decoder_1_c0, alpha_7seg_decoder_1_c1, alpha_7seg_decoder_1_c2, alpha_7seg_decoder_1_c3,
       alpha_7seg_decoder_1_c4, alpha_7seg_decoder_1_c5, alpha_7seg_decoder_1_c6;

  Alpha_7Seg_Decoder alpha_7seg_decoder_1 (
    .X(X), .Y(Y), .Z(Z), .C0(alpha_7seg_decoder_1_c0), .C1(alpha_7seg_decoder_1_c1),
    .C2(alpha_7seg_decoder_1_c2), .C3(alpha_7seg_decoder_1_c3), .C4(alpha_7seg_decoder_1_c4),
    .C5(alpha_7seg_decoder_1_c5), .C6(alpha_7seg_decoder_1_c6));
  _7_Segment_Display u_7_segment_display_1 (
    .g(alpha_7seg_decoder_1_c6), .f(alpha_7seg_decoder_1_c5), .a(alpha_7seg_decoder_1_c0),
    .b(alpha_7seg_decoder_1_c1), .e(alpha_7seg_decoder_1_c4), .d(alpha_7seg_decoder_1_c3),
    .c(alpha_7seg_decoder_1_c2));  // open: dp

  // Notes on the sheet:
  //   Alpha-7Seg-Decoder
endmodule

module Alpha_7Seg_Decoder (
  input  X,
  input  Y,
  input  Z,
  output C0,
  output C1,
  output C2,
  output C3,
  output C4,
  output C5,
  output C6
);

  wire not_1_out, not_2_out, not_3_out, X_prime_Y_out, X_prime_Y_prime_out, XY_prime_out, XZ_out,
       YZ_prime_out, Z_prime_X_prime_out, Z_prime_Y_prime_out;

  not not_1 (not_1_out, X);
  not not_2 (not_2_out, Y);
  not not_3 (not_3_out, Z);
  and X_prime_Y_prime (X_prime_Y_prime_out, not_1_out, not_2_out);
  and Z_prime_X_prime (Z_prime_X_prime_out, not_3_out, not_1_out);
  and Z_prime_Y_prime (Z_prime_Y_prime_out, not_3_out, not_2_out);
  and X_prime_Y (X_prime_Y_out, not_1_out, Y);
  and XY_prime (XY_prime_out, X, not_2_out);
  and YZ_prime (YZ_prime_out, Y, not_3_out);
  and XZ (XZ_out, X, Z);
  or or_1 (C1, X_prime_Y_prime_out, Z_prime_X_prime_out, Z_prime_Y_prime_out);
  or or_2 (C3, X_prime_Y_out, XY_prime_out);
  or or_3 (C6, X_prime_Y_prime_out, YZ_prime_out, XZ_out);

  assign C0 = 1'b1;
  assign C2 = C1;
  assign C4 = 1'b1;
  assign C5 = 1'b1;
endmodule
